// Logisim project blackjack_game.circ as structural Verilog: 11 circuits, main circuit main
module main (
);

  wire all_in, and_6_out, bet_1, bet_5, bet_20, clock_1_out, clock_2_out, clock_3_out, clock_4_out,
       clock_5_out, clock_6_out, comparator_1_gt, comparator_1_lt, comparator_2_gt, comparator_3_gt,
       diller_hit, diller_hit_main, diller_lose, diller_win, final_user_win, five_cards, HIT, hit_t, led1,
       led1_clk, led3, led_lose, led_lose_clk, led_win, led_win_clk, main_hit, New_g_or_r, new_game,
       newround, not_1_out, or_4_out, or_5_out, or_8_out, or_9_out, or_10_out, or_11_out, register_1_q,
       reset_money, stand, user_lose, user_win;
  wire [2:0] multiplexer_1_out;
  wire [3:0] bank1, bank10, bank100, bank1000, c_u1, c_u10, c_u100, c_u1000, diller1, diller10, s_r_d1,
       s_r_d10, s_r_u1, s_r_u10, User1, User10;
  wire [4:0] card_value;
  wire [7:0] count_diller_win, count_user_win, sum_res_diller, sum_res_user;
  wire [11:0] chips_sum, chips_user, sum_bet;
  wire [34:0] Card_Number, Card_Symbol, Scr_D_N1, Scr_D_N2, Scr_D_N3, Scr_D_N4, Scr_D_N5, Scr_D_S1, Scr_D_S2,
       Scr_D_S3, Scr_D_S4, Scr_D_S5, Scr_N1, Scr_N2, Scr_N3, Scr_N4, Scr_N5, Scr_S1, Scr_S2, Scr_S3, Scr_S4,
       Scr_S5;

  LED led_1 (.in(led_win_clk));
  LED led_2 (.in(led_lose_clk));
  LED led_3 (.in(led_lose_clk));
  LED led_4 (.in(led_lose_clk));
  LED led_5 (.in(led_lose_clk));
  LED led_6 (.in(led_lose_clk));
  LED led_7 (.in(led_lose_clk));
  LED led_8 (.in(led_lose_clk));
  LED led_9 (.in(led_lose_clk));
  LED led_10 (.in(led_lose_clk));
  LED led_11 (.in(led_lose_clk));
  LED led_12 (.in(led_lose_clk));
  LED led_13 (.in(led_lose_clk));
  LED led_14 (.in(led_lose_clk));
  LED led_15 (.in(led_lose_clk));
  LED led_16 (.in(led_lose_clk));
  LED led_17 (.in(led_lose_clk));
  LED led_18 (.in(led_lose_clk));
  LED led_19 (.in(led_lose_clk));
  LED led_20 (.in(led_lose_clk));
  LED led_21 (.in(led_lose_clk));
  LED led_22 (.in(led_lose_clk));
  LED led_23 (.in(led_lose_clk));
  LED led_24 (.in(led_lose_clk));
  LED led_25 (.in(led_lose_clk));
  LED led_26 (.in(led_lose_clk));
  LED led_27 (.in(led_lose_clk));
  LED led_28 (.in(led_win_clk));
  LED led_29 (.in(led_win_clk));
  LED led_30 (.in(led_win_clk));
  LED led_31 (.in(led_win_clk));
  Hex_Digit_Display hex_digit_display_1 (.value(c_u1000));  // open: dp
  Hex_Digit_Display hex_digit_display_2 (.value(c_u100));  // open: dp
  LED led_32 (.in(led_win_clk));
  LED led_33 (.in(led_win_clk));
  LED led_34 (.in(led_win_clk));
  LED led_35 (.in(led_win_clk));
  LED led_36 (.in(led_win_clk));
  LED led_37 (.in(led_win_clk));
  Hex_Digit_Display hex_digit_display_3 (.value(c_u10));  // open: dp
  Hex_Digit_Display hex_digit_display_4 (.value(c_u1));  // open: dp
  LED led_38 (.in(led3));
  LED led_39 (.in(led3));
  LED led_40 (.in(led3));
  LED led_41 (.in(led3));
  Button button_1 (.out(bet_1));
  Button button_2 (.out(all_in));
  LED led_42 (.in(led3));
  LED led_43 (.in(led3));
  LED led_44 (.in(led3));
  LED led_45 (.in(led3));
  LED led_46 (.in(led_win_clk));
  LED led_47 (.in(led_win_clk));
  LED led_48 (.in(led_win_clk));
  LED led_49 (.in(led_win_clk));
  LED led_50 (.in(led_win_clk));
  Button button_3 (.out(new_game));
  Hex_Digit_Display hex_digit_display_5 (.value(bank1000));  // open: dp
  LED led_51 (.in(led3));
  LED led_52 (.in(led3));
  LED led_53 (.in(led3));
  LED led_54 (.in(led3));
  Button button_4 (.out(bet_5));
  LED led_55 (.in(led3));
  LED led_56 (.in(led3));
  LED led_57 (.in(led3));
  LED led_58 (.in(led3));
  LED led_59 (.in(led_win_clk));
  LED led_60 (.in(led_win_clk));
  LED led_61 (.in(led_win_clk));
  LED led_62 (.in(led_win_clk));
  LED led_63 (.in(led_win_clk));
  Hex_Digit_Display hex_digit_display_6 (.value(bank100));  // open: dp
  Hex_Digit_Display hex_digit_display_7 (.value(bank10));  // open: dp
  LED led_64 (.in(led3));
  LED led_65 (.in(led3));
  LED led_66 (.in(led3));
  LED led_67 (.in(led3));
  Button button_5 (.out(bet_20));
  Button button_6 (.out(reset_money));
  LED led_68 (.in(led3));
  LED led_69 (.in(led3));
  LED led_70 (.in(led3));
  LED led_71 (.in(led3));
  LED led_72 (.in(led_win_clk));
  LED led_73 (.in(led_win_clk));
  LED led_74 (.in(led_win_clk));
  LED led_75 (.in(led_win_clk));
  LED led_76 (.in(led_win_clk));
  LED led_77 (.in(led_win_clk));
  Hex_Digit_Display hex_digit_display_8 (.value(bank1));  // open: dp
  LED led_78 (.in(led3));
  LED led_79 (.in(led3));
  LED led_80 (.in(led_win_clk));
  LED led_81 (.in(led_win_clk));
  LED led_82 (.in(led_win_clk));
  LED led_83 (.in(led_win_clk));
  LED led_84 (.in(led_win_clk));
  DotMatrix dotmatrix_1 (
    .col0(Scr_D_N1[34:28]), .col1(Scr_D_N1[27:21]), .col2(Scr_D_N1[20:14]), .col3(Scr_D_N1[13:7]),
    .col4(Scr_D_N1[6:0]));
  DotMatrix dotmatrix_2 (
    .col0(Scr_N1[34:28]), .col1(Scr_N1[27:21]), .col2(Scr_N1[20:14]), .col3(Scr_N1[13:7]), .col4(Scr_N1[6:0]));
  LED led_85 (.in(led_win_clk));
  LED led_86 (.in(led_win_clk));
  LED led_87 (.in(led_win_clk));
  LED led_88 (.in(led_win_clk));
  LED led_89 (.in(led_win_clk));
  LED led_90 (.in(led_lose));
  LED led_91 (.in(led_lose));
  LED led_92 (.in(led_lose));
  Hex_Digit_Display hex_digit_display_9 (.value(diller10));  // open: dp
  LED led_93 (.in(led_lose));
  LED led_94 (.in(led_lose));
  DotMatrix dotmatrix_3 (
    .col0(Scr_D_N2[34:28]), .col1(Scr_D_N2[27:21]), .col2(Scr_D_N2[20:14]), .col3(Scr_D_N2[13:7]),
    .col4(Scr_D_N2[6:0]));
  DotMatrix dotmatrix_4 (
    .col0(Scr_D_S1[34:28]), .col1(Scr_D_S1[27:21]), .col2(Scr_D_S1[20:14]), .col3(Scr_D_S1[13:7]),
    .col4(Scr_D_S1[6:0]));
  Button button_7 (.out(HIT));
  DotMatrix dotmatrix_5 (
    .col0(Scr_N2[34:28]), .col1(Scr_N2[27:21]), .col2(Scr_N2[20:14]), .col3(Scr_N2[13:7]), .col4(Scr_N2[6:0]));
  DotMatrix dotmatrix_6 (
    .col0(Scr_S1[34:28]), .col1(Scr_S1[27:21]), .col2(Scr_S1[20:14]), .col3(Scr_S1[13:7]), .col4(Scr_S1[6:0]));
  LED led_95 (.in(led_win_clk));
  LED led_96 (.in(led_win_clk));
  LED led_97 (.in(led_win_clk));
  LED led_98 (.in(led_win_clk));
  LED led_99 (.in(led_win_clk));
  LED led_100 (.in(led_win_clk));
  Hex_Digit_Display hex_digit_display_10 (.value(diller1));  // open: dp
  LED led_101 (.in(led_lose));
  LED led_102 (.in(led_lose));
  LED led_103 (.in(led_lose));
  LED led_104 (.in(led_lose));
  DotMatrix dotmatrix_7 (
    .col0(Scr_D_S2[34:28]), .col1(Scr_D_S2[27:21]), .col2(Scr_D_S2[20:14]), .col3(Scr_D_S2[13:7]),
    .col4(Scr_D_S2[6:0]));
  DotMatrix dotmatrix_8 (
    .col0(Scr_S2[34:28]), .col1(Scr_S2[27:21]), .col2(Scr_S2[20:14]), .col3(Scr_S2[13:7]), .col4(Scr_S2[6:0]));
  LED led_105 (.in(led_win_clk));
  LED led_106 (.in(led_win_clk));
  LED led_107 (.in(led_win_clk));
  LED led_108 (.in(led_win_clk));
  LED led_109 (.in(led_win_clk));
  LED led_110 (.in(led_lose));
  LED led_111 (.in(led_lose));
  LED led_112 (.in(led_lose));
  DotMatrix dotmatrix_9 (
    .col0(Scr_D_N3[34:28]), .col1(Scr_D_N3[27:21]), .col2(Scr_D_N3[20:14]), .col3(Scr_D_N3[13:7]),
    .col4(Scr_D_N3[6:0]));
  LED led_113 (.in(led1_clk));
  LED led_114 (.in(led1_clk));
  LED led_115 (.in(led1_clk));
  LED led_116 (.in(led1_clk));
  LED led_117 (.in(led1_clk));
  Button button_8 (.out(newround));
  LED led_118 (.in(led1_clk));
  LED led_119 (.in(led1_clk));
  LED led_120 (.in(led1_clk));
  LED led_121 (.in(led1_clk));
  LED led_122 (.in(led1_clk));
  DotMatrix dotmatrix_10 (
    .col0(Scr_N3[34:28]), .col1(Scr_N3[27:21]), .col2(Scr_N3[20:14]), .col3(Scr_N3[13:7]), .col4(Scr_N3[6:0]));
  LED led_123 (.in(led_win_clk));
  LED led_124 (.in(led_win_clk));
  LED led_125 (.in(led_win_clk));
  LED led_126 (.in(led_win_clk));
  LED led_127 (.in(led_win_clk));
  LED led_128 (.in(led_win));
  LED led_129 (.in(led_win));
  LED led_130 (.in(led_win));
  Hex_Digit_Display hex_digit_display_11 (.value(User10));  // open: dp
  LED led_131 (.in(led_win));
  LED led_132 (.in(led_win));
  LED led_133 (.in(led_win));
  DotMatrix dotmatrix_11 (
    .col0(Scr_D_S3[34:28]), .col1(Scr_D_S3[27:21]), .col2(Scr_D_S3[20:14]), .col3(Scr_D_S3[13:7]),
    .col4(Scr_D_S3[6:0]));
  DotMatrix dotmatrix_12 (
    .col0(Scr_D_N4[34:28]), .col1(Scr_D_N4[27:21]), .col2(Scr_D_N4[20:14]), .col3(Scr_D_N4[13:7]),
    .col4(Scr_D_N4[6:0]));
  LED led_134 (.in(led1_clk));
  LED led_135 (.in(led1_clk));
  LED led_136 (.in(led1_clk));
  LED led_137 (.in(led1_clk));
  LED led_138 (.in(led1_clk));
  LED led_139 (.in(led1_clk));
  DotMatrix dotmatrix_13 (
    .col0(Scr_S3[34:28]), .col1(Scr_S3[27:21]), .col2(Scr_S3[20:14]), .col3(Scr_S3[13:7]), .col4(Scr_S3[6:0]));
  DotMatrix dotmatrix_14 (
    .col0(Scr_N4[34:28]), .col1(Scr_N4[27:21]), .col2(Scr_N4[20:14]), .col3(Scr_N4[13:7]), .col4(Scr_N4[6:0]));
  LED led_140 (.in(led_win_clk));
  LED led_141 (.in(led_win_clk));
  LED led_142 (.in(led_win_clk));
  LED led_143 (.in(led_win_clk));
  LED led_144 (.in(led_win_clk));
  LED led_145 (.in(led_win_clk));
  LED led_146 (.in(led_win));
  LED led_147 (.in(led_win));
  LED led_148 (.in(led_win));
  Hex_Digit_Display hex_digit_display_12 (.value(User1));  // open: dp
  LED led_149 (.in(led_win));
  LED led_150 (.in(led_win));
  LED led_151 (.in(led_win));
  DotMatrix dotmatrix_15 (
    .col0(Scr_D_S4[34:28]), .col1(Scr_D_S4[27:21]), .col2(Scr_D_S4[20:14]), .col3(Scr_D_S4[13:7]),
    .col4(Scr_D_S4[6:0]));
  DotMatrix dotmatrix_16 (
    .col0(Scr_S4[34:28]), .col1(Scr_S4[27:21]), .col2(Scr_S4[20:14]), .col3(Scr_S4[13:7]), .col4(Scr_S4[6:0]));
  LED led_152 (.in(led_win_clk));
  LED led_153 (.in(led_win_clk));
  LED led_154 (.in(led_win_clk));
  LED led_155 (.in(led_win_clk));
  LED led_156 (.in(led_win_clk));
  DotMatrix dotmatrix_17 (
    .col0(Scr_D_N5[34:28]), .col1(Scr_D_N5[27:21]), .col2(Scr_D_N5[20:14]), .col3(Scr_D_N5[13:7]),
    .col4(Scr_D_N5[6:0]));
  Button button_9 (.out(stand));
  DotMatrix dotmatrix_18 (
    .col0(Scr_N5[34:28]), .col1(Scr_N5[27:21]), .col2(Scr_N5[20:14]), .col3(Scr_N5[13:7]), .col4(Scr_N5[6:0]));
  LED led_157 (.in(led_win_clk));
  LED led_158 (.in(led_win_clk));
  LED led_159 (.in(led_win_clk));
  LED led_160 (.in(led_win_clk));
  LED led_161 (.in(led_win_clk));
  DotMatrix dotmatrix_19 (
    .col0(Scr_D_S5[34:28]), .col1(Scr_D_S5[27:21]), .col2(Scr_D_S5[20:14]), .col3(Scr_D_S5[13:7]),
    .col4(Scr_D_S5[6:0]));
  DotMatrix dotmatrix_20 (
    .col0(Scr_S5[34:28]), .col1(Scr_S5[27:21]), .col2(Scr_S5[20:14]), .col3(Scr_S5[13:7]), .col4(Scr_S5[6:0]));
  LED led_162 (.in(led_win_clk));
  LED led_163 (.in(led_win_clk));
  LED led_164 (.in(led_win_clk));
  LED led_165 (.in(led_win_clk));
  LED led_166 (.in(led_win_clk));
  LED led_167 (.in(led_win_clk));
  Hex_Digit_Display hex_digit_display_13 (.value(s_r_d10), .dp(s_r_d10[0]));
  Hex_Digit_Display hex_digit_display_14 (.value(s_r_d1));  // open: dp
  Hex_Digit_Display hex_digit_display_15 (.value(s_r_u10));  // open: dp
  Hex_Digit_Display hex_digit_display_16 (.value(s_r_u1));  // open: dp
  LED led_168 (.in(led_win_clk));
  LED led_169 (.in(led_win_clk));
  LED led_170 (.in(led_win_clk));
  LED led_171 (.in(led_win_clk));
  LED led_172 (.in(led_win_clk));
  LED led_173 (.in(led_win_clk));
  LED led_174 (.in(led_win_clk));
  LED led_175 (.in(led_win_clk));
  LED led_176 (.in(led_lose_clk));
  LED led_177 (.in(led_lose_clk));
  LED led_178 (.in(led_lose_clk));
  LED led_179 (.in(led_lose_clk));
  LED led_180 (.in(led_lose_clk));
  LED led_181 (.in(led_lose_clk));
  LED led_182 (.in(led_lose_clk));
  LED led_183 (.in(led_lose_clk));
  LED led_184 (.in(led_lose_clk));
  LED led_185 (.in(led_lose_clk));
  LED led_186 (.in(led_lose_clk));
  LED led_187 (.in(led_lose_clk));
  LED led_188 (.in(led_lose_clk));
  LED led_189 (.in(led_lose_clk));
  LED led_190 (.in(led_lose_clk));
  LED led_191 (.in(led_lose_clk));
  LED led_192 (.in(led_lose_clk));
  LED led_193 (.in(led_lose_clk));
  LED led_194 (.in(led_lose_clk));
  LED led_195 (.in(led_lose_clk));
  LED led_196 (.in(led_lose_clk));
  LED led_197 (.in(led_lose_clk));
  LED led_198 (.in(led_lose_clk));
  LED led_199 (.in(led_lose_clk));
  LED led_200 (.in(led_lose_clk));
  LED led_201 (.in(led_lose_clk));
  LED led_202 (.in(led_win_clk));
  or or_1 (led_win, final_user_win, diller_lose);
  or or_2 (led_lose, diller_win, user_lose);
  Multiplexer #(.select(2), .width(3)) multiplexer_1 (
    .in0(3'b000), .in1(3'b001), .in2(3'b010), .in3(3'b000), .out(multiplexer_1_out), .sel({led_win, led_lose}));
  or or_3 (led1, led_win, led_lose);
  Clock clock_1 (.out(clock_1_out));
  and and_1 (led_lose_clk, led_lose, clock_2_out);
  Clock clock_2 (.out(clock_2_out));
  and and_2 (led_win_clk, led_win, clock_3_out);
  Clock clock_3 (.out(clock_3_out));
  Comparator #(.width(12)) comparator_1 (
    .a(chips_sum), .b(sum_bet), .gt(comparator_1_gt), .lt(comparator_1_lt));  // open: eq
  and and_3 (led1_clk, led1, clock_1_out);
  Register #(.trigger("high"), .width(1)) register_1 (
    .D(or_4_out), .clk(or_4_out), .Q(register_1_q), .clr(HIT));  // open: en
  or or_4 (or_4_out, newround, new_game);
  not not_1 (not_1_out, comparator_1_lt);
  Clock clock_4 (.out(clock_4_out));
  Multiplexer #(.width(12)) multiplexer_2 (.in0(chips_sum), .in1(sum_bet), .out(chips_user), .sel(not_1_out));
  and and_4 (led3, register_1_q, clock_4_out);
  Comparator #(.width(12)) comparator_2 (.a(sum_bet), .b({12{1'b0}}), .gt(comparator_2_gt));  // open: eq, lt
  Bank bank_1 (.Bet(chips_user), .game(multiplexer_1_out), .new_round(newround), .Resat(new_game), .Sum_sof(chips_sum));
  and and_5 (main_hit, HIT, comparator_2_gt);
  // Binary_to_BCD_converter #(.binvalue(12)) binary_to_bcd_converter_1: pin names not known; wires that end beside it: chips_sum, bank1000, bank100, bank10
  // Binary_to_BCD_converter #(.binvalue(8)) binary_to_bcd_converter_2: pin names not known; wires that end beside it: count_user_win, User10, User1
  // Binary_to_BCD_converter #(.binvalue(8)) binary_to_bcd_converter_3: pin names not known; wires that end beside it: count_diller_win, diller10, diller1
  or or_5 (or_5_out, hit_t, diller_hit);
  Clock clock_5 (.out(clock_5_out));
  // Binary_to_BCD_converter #(.binvalue(12)) binary_to_bcd_converter_4: pin names not known; wires that end beside it: bank1, chips_user, c_u1000, c_u100, c_u10, c_u1
  // Binary_to_BCD_converter #(.binvalue(8)) binary_to_bcd_converter_5: pin names not known; wires that end beside it: sum_res_user, s_r_u10, s_r_u1
  // Binary_to_BCD_converter #(.binvalue(8)) binary_to_bcd_converter_6: pin names not known; wires that end beside it: sum_res_diller, s_r_d10, s_r_d1
  cards cards_1 (
    .hit(or_5_out), .clock1(clock_5_out), .clock2(clock_5_out), .Card_Number(Card_Number),
    .Card_Symbol(Card_Symbol), .card_value(card_value));
  bet u_bet_1 (
    .bet1(bet_1), .bet5(bet_5), .bet20(bet_20), .temp(chips_sum), .Reset(new_game),
    .Reset_money(reset_money), .All_in(all_in), .Sum_bet(sum_bet));
  Comparator comparator_3 (.a(sum_res_user), .b(sum_res_diller), .gt(comparator_3_gt));  // open: eq, lt
  and and_6 (and_6_out, five_cards, comparator_3_gt);
  Clock clock_6 (.out(clock_6_out));
  or or_6 (final_user_win, user_win, and_6_out);
  or or_7 (New_g_or_r, newround, new_game);
  or or_8 (or_8_out, diller_win, user_lose);
  or or_9 (or_9_out, user_win, diller_lose);
  or or_10 (or_10_out, or_8_out, or_9_out);
  count_win_lose count_win_lose_1 (
    .hit(newround), .user_win(final_user_win), .diller_lose(diller_lose), .diller_win(diller_win),
    .user_lose(user_lose), .new_game(new_game), .count_user_win(count_user_win),
    .count_diller_win(count_diller_win));
  diller diller_1 (
    .stand(stand), .new_round(newround), .new_game(new_game), .diller_clock(clock_6_out),
    .diller_hit(diller_hit_main));
  win_lose_diller win_lose_diller_1 (
    .sum_cards_diller(sum_res_diller), .sum_cards_user(sum_res_user), .diller_lose(diller_lose),
    .diller_win(diller_win));
  win_lose win_lose_1 (.sum_cards_user(sum_res_user), .user_lose(user_lose), .user_win(user_win));
  or or_11 (or_11_out, New_g_or_r, stand);
  Control_Hit_Cards control_hit_cards_1 (
    .hit(main_hit), .newround(New_g_or_r), .user_lose(or_10_out), .user_hit(hit_t));  // open: five_cards
  Control_Hit_Cards control_hit_cards_2 (
    .hit(diller_hit_main), .newround(or_11_out), .user_lose(or_10_out), .five_cards(five_cards),
    .user_hit(diller_hit));
  SUM_CARDS sum_cards_1 (.hit(hit_t), .new_round(New_g_or_r), .card_value(card_value), .sum_res(sum_res_user));
  SUM_CARDS sum_cards_2 (.hit(diller_hit), .new_round(New_g_or_r), .card_value(card_value), .sum_res(sum_res_diller));
  save_cards_to_lcd save_cards_to_lcd_1 (
    .Card_Number(Card_Number), .stand(stand), .rst(New_g_or_r), .Card_Symbol(Card_Symbol), .hit(hit_t),
    .diller_hit(diller_hit), .Scr_N1(Scr_N1), .Scr_S1(Scr_S1), .Scr_N2(Scr_N2), .Scr_S2(Scr_S2),
    .Scr_N3(Scr_N3), .Scr_S3(Scr_S3), .Scr_N4(Scr_N4), .Scr_S4(Scr_S4), .Scr_N5(Scr_N5), .Scr_S5(Scr_S5),
    .Scr_D_N1(Scr_D_N1), .Scr_D_S1(Scr_D_S1), .Scr_D_N2(Scr_D_N2), .Scr_D_S2(Scr_D_S2), .Scr_D_N3(Scr_D_N3),
    .Scr_D_S3(Scr_D_S3), .Scr_D_N4(Scr_D_N4), .Scr_D_S4(Scr_D_S4), .Scr_D_N5(Scr_D_N5), .Scr_D_S5(Scr_D_S5));
  // Pins of 1 and 4 bits meet at s_r_d10

  // Notes on the sheet:
  //   סכום הימור
  //   התחל משחק חדש
  //   הכנס סכום הימור
  //   בנק השחקן
  //   משחק בלאק ג'ק
  //   מספר הפסדים
  //   קלפי הדילר
  //   לחץ על תחילת סבב חדש
  //   קלפי השחקן
  //   מספר ניצחונות
  //   סכום קלפי הדילר
  //   סכום קלפי המשתמש
  //   bank chips
  //   diller win points
  //   user win points
  //   sum_res_diller
  //   bank chips
  //   sum_res_user
endmodule

module SUM_CARDS (
  input  hit,
  input  new_round,
  input  [4:0] card_value,
  output [7:0] sum_res
);

  wire comparator_1_eq, comparator_1_lt, comparator_2_gt;
  wire [4:0] adder_2_out, multiplexer_1_out, multiplexer_2_out, multiplexer_3_out, multiplier_1_out;
  wire [7:0] adder_1_out, adder_3_out;

  // Probe on sum_res
  Adder adder_1 (.a(sum_res), .b({3'b000, adder_2_out}), .out(adder_1_out));  // open: cin, cout
  Comparator #(.width(5)) comparator_1 (
    .a(card_value), .b(5'b01011), .eq(comparator_1_eq), .lt(comparator_1_lt));  // open: gt
  Adder #(.width(5)) adder_2 (.a(multiplier_1_out), .b(multiplexer_2_out), .out(adder_2_out));  // open: cin, cout
  Multiplexer #(.width(5)) multiplexer_1 (
    .in0({5{1'b0}}), .in1(5'b00001), .out(multiplexer_1_out), .sel(comparator_1_eq));
  Register register_1 (.D(adder_1_out), .en(1'b1), .clk(hit), .Q(sum_res), .clr(new_round));
  Multiplexer #(.width(5)) multiplexer_2 (
    .in0({5{1'b0}}), .in1(card_value), .out(multiplexer_2_out), .sel(comparator_1_lt));
  // Probe on sum_res
  Multiplier #(.width(5)) multiplier_1 (
    .a(multiplexer_1_out), .b(multiplexer_3_out), .out(multiplier_1_out));  // open: cin, cout
  Adder adder_3 (.a(8'hb), .b(sum_res), .out(adder_3_out));  // open: cin, cout
  Comparator comparator_2 (.a(adder_3_out), .b(8'h15), .gt(comparator_2_gt));  // open: eq, lt
  Multiplexer #(.width(5)) multiplexer_3 (
    .in0(card_value), .in1(5'b00001), .out(multiplexer_3_out), .sel(comparator_2_gt));

  // Notes on the sheet:
  //   11
  //   0
  //   1
  //   1
  //   11
  //   SUM_CARDS+DEAL WITH AS CARD
  //   21
endmodule

module win_lose (
  input  [7:0] sum_cards_user,
  output user_lose,
  output user_win
);

  wire comparator_1_gt, comparator_1_lt;

  Comparator comparator_1 (.a(sum_cards_user), .b(8'h15), .gt(comparator_1_gt), .lt(comparator_1_lt));  // open: eq
  // Probe on comparator_1_lt
  Multiplexer multiplexer_1 (.in0(1'b0), .in1(1'b1), .out(user_lose), .sel(comparator_1_gt));
  xnor xnor_1 (user_win, user_lose, comparator_1_lt);
  // Probe on user_lose
  // Probe on user_win

  // Notes on the sheet:
  //   block user (stand =0) 
  //   user
  //   00=proceed_game
  //   10=lose higher 21
  //   01=equal 21=win
  //   go to diller count
  //   go to user count
endmodule

module win_lose_diller (
  input  [7:0] sum_cards_diller,
  input  [7:0] sum_cards_user,
  output diller_lose,
  output diller_win
);

  wire and_1_out, comparator_1_gt, comparator_1_lt, comparator_2_eq, comparator_2_lt, multiplexer_2_out,
       or_1_out, xnor_1_out, xnor_2_out;

  Comparator comparator_1 (.a(sum_cards_diller), .b(8'h15), .gt(comparator_1_gt), .lt(comparator_1_lt));  // open: eq
  // Probe on comparator_1_lt
  Multiplexer multiplexer_1 (.in0(1'b0), .in1(1'b1), .out(diller_lose), .sel(comparator_1_gt));
  Comparator comparator_2 (
    .a(sum_cards_diller), .b(sum_cards_user), .eq(comparator_2_eq), .lt(comparator_2_lt));  // open: gt
  xnor xnor_1 (xnor_1_out, diller_lose, comparator_1_lt);
  or or_1 (or_1_out, comparator_2_eq, comparator_2_lt);
  // Probe on or_1_out
  // Probe on diller_lose
  xnor xnor_2 (xnor_2_out, xnor_1_out, diller_lose);
  Multiplexer multiplexer_2 (.in0(1'b1), .in1(1'b0), .out(multiplexer_2_out), .sel(or_1_out));
  // Probe on xnor_1_out
  and and_1 (and_1_out, xnor_2_out, multiplexer_2_out);
  // Probe on and_1_out
  or or_2 (diller_win, xnor_1_out, and_1_out);

  // Notes on the sheet:
  //   block diller (stand =1)
  //   user
  //   go to user count 
  //   00=check if diller value higher from user
  //   10=diller lose  higher 21
  //   01=diller win equal 21=win
  //   go to diller count 
  //   1=diller win
  //   go to diller count 
endmodule

module count_win_lose (
  input  hit,
  input  user_win,
  input  diller_lose,
  input  diller_win,
  input  user_lose,
  input  new_game,
  output [7:0] count_user_win,
  output [7:0] count_diller_win
);

  wire nor_1_out, nor_2_out;
  wire [7:0] adder_1_out, adder_2_out, bitselector_1_out, bitselector_2_out;

  // Probe on bitselector_2_out
  nor nor_1 (nor_1_out, user_win, diller_lose);
  BitSelector #(.group(8), .width(1)) bitselector_1 (.in(1'b1), .out(bitselector_1_out), .sel(nor_2_out));
  nor nor_2 (nor_2_out, diller_win, user_lose);
  BitSelector #(.group(8), .width(1)) bitselector_2 (.in(1'b1), .out(bitselector_2_out), .sel(nor_1_out));
  // Probe on bitselector_1_out
  Adder adder_1 (.a(count_user_win), .b(bitselector_2_out), .out(adder_1_out));  // open: cin, cout
  Adder adder_2 (.a(count_diller_win), .b(bitselector_1_out), .out(adder_2_out));  // open: cin, cout
  Register register_1 (.D(adder_1_out), .en(1'b1), .clk(hit), .Q(count_user_win), .clr(new_game));
  Register register_2 (.D(adder_2_out), .en(1'b1), .clk(hit), .Q(count_diller_win), .clr(new_game));

  // Notes on the sheet:
  //   user
  //   diller
endmodule

module diller (
  input  stand,
  input  new_round,
  input  new_game,
  input  diller_clock,
  output diller_hit
);

  wire d_ff_1_q, or_1_out;

  or or_1 (or_1_out, new_round, new_game);
  D_Flip_Flop d_ff_1 (.D(stand), .clk(stand), .Q(d_ff_1_q), .reset(or_1_out));  // open: Qn, preset
  and and_1 (diller_hit, d_ff_1_q, diller_clock);
endmodule

module save_cards_to_lcd (
  input  [34:0] Card_Number,
  input  stand,
  input  rst,
  input  [34:0] Card_Symbol,
  input  hit,
  input  diller_hit,
  output [34:0] Scr_N1,
  output [34:0] Scr_S1,
  output [34:0] Scr_N2,
  output [34:0] Scr_S2,
  output [34:0] Scr_N3,
  output [34:0] Scr_S3,
  output [34:0] Scr_N4,
  output [34:0] Scr_S4,
  output [34:0] Scr_N5,
  output [34:0] Scr_S5,
  output [34:0] Scr_D_N1,
  output [34:0] Scr_D_S1,
  output [34:0] Scr_D_N2,
  output [34:0] Scr_D_S2,
  output [34:0] Scr_D_N3,
  output [34:0] Scr_D_S3,
  output [34:0] Scr_D_N4,
  output [34:0] Scr_D_S4,
  output [34:0] Scr_D_N5,
  output [34:0] Scr_D_S5
);

  wire and_1_out, ctr1, multiplexer_1_out, multiplexer_2_out;

  Multiplexer multiplexer_1 (.in0(1'b1), .in1(1'b0), .out(multiplexer_1_out), .sel(ctr1));
  Multiplexer multiplexer_2 (.in0(1'b0), .in1(diller_hit), .out(multiplexer_2_out), .sel(ctr1));
  and and_1 (and_1_out, hit, multiplexer_1_out);
  Register #(.width(35)) register_1 (.D(Card_Number), .clk(and_1_out), .Q(Scr_N1), .clr(rst));  // open: en
  Register #(.width(35)) register_2 (.D(Card_Number), .clk(multiplexer_2_out), .Q(Scr_D_N1), .clr(rst));  // open: en
  Register #(.width(35)) register_3 (.D(Scr_N1), .clk(and_1_out), .Q(Scr_N2), .clr(rst));  // open: en
  Register #(.width(35)) register_4 (.D(Scr_D_N1), .clk(multiplexer_2_out), .Q(Scr_D_N2), .clr(rst));  // open: en
  D_Flip_Flop d_ff_1 (.D(stand), .clk(stand), .Q(ctr1), .reset(rst));  // open: Qn, preset
  Register #(.width(35)) register_5 (.D(Scr_N2), .clk(and_1_out), .Q(Scr_N3), .clr(rst));  // open: en
  Register #(.width(35)) register_6 (.D(Scr_D_N2), .clk(multiplexer_2_out), .Q(Scr_D_N3), .clr(rst));  // open: en
  Register #(.width(35)) register_7 (.D(Scr_N3), .clk(and_1_out), .Q(Scr_N4), .clr(rst));  // open: en
  Register #(.width(35)) register_8 (.D(Scr_D_N3), .clk(multiplexer_2_out), .Q(Scr_D_N4), .clr(rst));  // open: en
  Register #(.width(35)) register_9 (.D(Scr_N4), .clk(and_1_out), .Q(Scr_N5), .clr(rst));  // open: en
  Register #(.width(35)) register_10 (.D(Scr_D_N4), .clk(multiplexer_2_out), .Q(Scr_D_N5), .clr(rst));  // open: en
  Register #(.width(35)) register_11 (.D(Card_Symbol), .clk(and_1_out), .Q(Scr_S1), .clr(rst));  // open: en
  Register #(.width(35)) register_12 (.D(Card_Symbol), .clk(multiplexer_2_out), .Q(Scr_D_S1), .clr(rst));  // open: en
  Register #(.width(35)) register_13 (.D(Scr_S1), .clk(and_1_out), .Q(Scr_S2), .clr(rst));  // open: en
  Register #(.width(35)) register_14 (.D(Scr_D_S1), .clk(multiplexer_2_out), .Q(Scr_D_S2), .clr(rst));  // open: en
  Register #(.width(35)) register_15 (.D(Scr_S2), .clk(and_1_out), .Q(Scr_S3), .clr(rst));  // open: en
  Register #(.width(35)) register_16 (.D(Scr_D_S2), .clk(multiplexer_2_out), .Q(Scr_D_S3), .clr(rst));  // open: en
  Register #(.width(35)) register_17 (.D(Scr_S3), .clk(and_1_out), .Q(Scr_S4), .clr(rst));  // open: en
  Register #(.width(35)) register_18 (.D(Scr_D_S3), .clk(multiplexer_2_out), .Q(Scr_D_S4), .clr(rst));  // open: en
  Register #(.width(35)) register_19 (.D(Scr_S4), .clk(and_1_out), .Q(Scr_S5), .clr(rst));  // open: en
  Register #(.width(35)) register_20 (.D(Scr_D_S4), .clk(multiplexer_2_out), .Q(Scr_D_S5), .clr(rst));  // open: en
endmodule

module cards (
  input  hit,
  input  clock1,
  input  clock2,
  output [34:0] Card_Number,
  output [34:0] Card_Symbol,
  output [4:0] card_value
);

  wire and_1_out, and_2_out, counter_1_carry, not_1_out, not_2_out, or_1_out, or_2_out, or_3_out, undriven;
  wire [1:0] register_1_q_2;
  wire [4:1] register_1_q;
  wire [5:0] counter_1_q, shift_register_1_p11;
  wire [51:35] rom_1_data;

  not not_1 (not_1_out, or_3_out);
  and and_1 (and_1_out, counter_1_carry, clock2);
  and and_2 (and_2_out, not_1_out, clock2);
  Counter #(.max('h3f), .width(6)) counter_1 (
    .clr(and_1_out), .up(1'b1), .count(1'b1), .clk(and_2_out), .D({6{1'b0}}), .carry(counter_1_carry),
    .Q(counter_1_q));  // open: load
  not not_2 (not_2_out, or_3_out);
  Register #(.width(6)) register_1 (
    .D(shift_register_1_p11), .en(1'b1), .clk(hit), .Q({register_1_q_2[1], register_1_q, register_1_q_2[0]}),
    .clr(undriven));
  ROM #(.addrWidth(6), .dataWidth(52)) rom_1 (
    .addr({register_1_q_2[1], register_1_q, register_1_q_2[0]}),
    .data({rom_1_data[51:49], card_value, rom_1_data[43:35], Card_Number[6:0], Card_Number[13:7], Card_Number[20:14], Card_Number[27:21], Card_Number[34:28]}));
  // Shift_Register #(.length(6)) shift_register_1: pin names not known; wires that end beside it: 1'b0, not_2_out, clock1, 1'b0, counter_1_q[0], counter_1_q[1], counter_1_q[2], counter_1_q[3], counter_1_q[4], counter_1_q[5], shift_register_1_p11[0], shift_register_1_p11[1], shift_register_1_p11[2], shift_register_1_p11[3], shift_register_1_p11[4], shift_register_1_p11[5]
  DotMatrix dotmatrix_1 (
    .col0(Card_Number[34:28]), .col1(Card_Number[27:21]), .col2(Card_Number[20:14]),
    .col3(Card_Number[13:7]), .col4(Card_Number[6:0]));
  ROM #(.addrWidth(2), .dataWidth(35)) rom_2 (
    .addr(register_1_q_2),
    .data({Card_Symbol[6:0], Card_Symbol[13:7], Card_Symbol[20:14], Card_Symbol[27:21], Card_Symbol[34:28]}));
  or or_1 (or_1_out, shift_register_1_p11[0], shift_register_1_p11[1], shift_register_1_p11[2]);
  or or_2 (or_2_out, shift_register_1_p11[3], shift_register_1_p11[4], shift_register_1_p11[5]);
  DotMatrix dotmatrix_2 (
    .col0(Card_Symbol[34:28]), .col1(Card_Symbol[27:21]), .col2(Card_Symbol[20:14]),
    .col3(Card_Symbol[13:7]), .col4(Card_Symbol[6:0]));
  or or_3 (or_3_out, or_1_out, or_2_out);

  // Notes on the sheet:
  //   contents of rom_1 (hex, n*v repeats v):
  //   b00007ca1f00 2000074a9700 300007ca9500 400007c21c00 500005ca9d00 600005ca9f00 7000060b9000
  //   800007ca9f00 900007ca9d00 a003e44f803e a00207c88300 a00027c89f00 a00222821f00 b00007ca1f00
  //   2000074a9700 300007ca9500 400007c21c00 500005ca9d00 600005ca9f00 7000060b9000 800007ca9f00
  //   900007ca9d00 a003e44f803e a00207c88300 a00027c89f00 a00222821f00 b00007ca1f00 2000074a9700
  //   300007ca9500 400007c21c00 500005ca9d00 600005ca9f00 7000060b9000 800007ca9f00 900007ca9d00
  //   a003e44f803e a00207c88300 a00027c89f00 a00222821f00 b00007ca1f00 2000074a9700 300007ca9500
  //   400007c21c00 500005ca9d00 600005ca9f00 7000060b9000 800007ca9f00 900007ca9d00 a003e44f803e
  //   a00207c88300 a00027c89f00 a00222821f00 b00007ca1f00 2000074a9700 300007ca9500 400007c21c00
  //   500005ca9d00 600005ca9f00 7000060b9000 800007ca9f00 900007ca9d00 a003e44f803e a00207c88300
  //   a00027c89f00
  //   contents of rom_2 (hex, n*v repeats v):
  //   387879e38 c3cfcf0c 1c50fd41c 1871f9c18
endmodule

module bet (
  input  bet1,
  input  bet5,
  input  bet20,
  input  [11:0] temp,
  input  Reset,
  input  Reset_money,
  input  All_in,
  output [11:0] Sum_bet
);

  wire d_ff_1_q, or_1_out, or_2_out;
  wire [1:0] priority_encoder_1_out;
  wire [11:0] adder_1_out, multiplexer_1_out, register_1_q;

  Priority_Encoder #(.select(2)) priority_encoder_1 (
    .in0(1'b1), .in1(bet1), .in2(bet5), .in3(bet20), .out(priority_encoder_1_out));  // open: gs, en_out, en_in
  or or_1 (or_1_out, bet1, bet5, bet20);
  Multiplexer #(.select(2), .width(12)) multiplexer_1 (
    .in0({12{1'b0}}), .in1(12'h1), .in2(12'h5), .in3(12'h14), .out(multiplexer_1_out),
    .sel(priority_encoder_1_out));
  Adder #(.width(12)) adder_1 (.a(register_1_q), .b(multiplexer_1_out), .out(adder_1_out));  // open: cin, cout
  or or_2 (or_2_out, Reset, Reset_money);
  Register #(.trigger("falling"), .width(12)) register_1 (
    .D(adder_1_out), .en(1'b1), .clk(or_1_out), .Q(register_1_q), .clr(or_2_out));
  D_Flip_Flop d_ff_1 (.D(All_in), .clk(All_in), .Q(d_ff_1_q), .reset(or_2_out));  // open: Qn, preset
  Multiplexer #(.width(12)) multiplexer_2 (.in0(register_1_q), .in1(temp), .out(Sum_bet), .sel(d_ff_1_q));
endmodule

module Bank (
  input  [11:0] Bet,
  input  [2:0] game,
  input  new_round,
  input  Resat,
  output [11:0] Sum_sof
);

  wire counter_1_carry, not_1_out, or_1_out;
  wire [1:0] multiplexer_1_out;
  wire [2:2] multiplexer_1_out_2;
  wire [11:0] adder_1_out, multiplexer_2_out, subtractor_1_out;

  // Probe on Bet
  Subtractor #(.width(12)) subtractor_1 (.a(Sum_sof), .b(Bet), .out(subtractor_1_out));  // open: bin, bout
  // Probe on adder_1_out
  Adder #(.width(12)) adder_1 (.a(Bet), .b(Sum_sof), .out(adder_1_out));  // open: cin, cout
  Multiplexer #(.width(3)) multiplexer_1 (
    .in0(game), .in1(3'b011), .out({multiplexer_1_out_2[2], multiplexer_1_out}), .sel(Resat));
  Multiplexer #(.select(2), .width(12)) multiplexer_2 (
    .in0(Sum_sof), .in1(subtractor_1_out), .in2(adder_1_out), .in3(12'hc8), .out(multiplexer_2_out),
    .sel(multiplexer_1_out));
  Counter #(.max('h1), .width(1)) counter_1 (.up(Resat), .carry(counter_1_carry));  // open: clr, load, count, clk, D, Q
  Register #(.width(12)) register_1 (.D(multiplexer_2_out), .en(1'b1), .clk(or_1_out), .Q(Sum_sof));  // open: clr
  or or_1 (or_1_out, not_1_out, new_round);
  not not_1 (not_1_out, counter_1_carry);

  // Other names for the same wires on the sheet: Temp[11:0] = Sum_sof

  // Notes on the sheet:
  //   game: initial=0x3
endmodule

module Control_Hit_Cards (
  input  hit,
  input  newround,
  input  user_lose,
  output five_cards,
  output user_hit
);

  wire and_1_out, nand_1_out, not_1_out;
  wire [3:0] adder_1_out, bitselector_1_out, register_1_q;

  BitSelector #(.group(4), .width(1)) bitselector_1 (.in(1'b1), .out(bitselector_1_out), .sel(hit));
  and and_1 (and_1_out, hit, user_hit);
  Adder #(.width(4)) adder_1 (.a(register_1_q), .b(bitselector_1_out), .out(adder_1_out));  // open: cin, cout
  Register #(.width(4)) register_1 (.D(adder_1_out), .en(1'b1), .clk(and_1_out), .Q(register_1_q), .clr(newround));
  Comparator #(.width(4)) comparator_1 (.a(register_1_q), .b(4'b0100), .gt(five_cards));  // open: eq, lt
  not not_1 (not_1_out, five_cards);
  // Probe on not_1_out
  nand nand_1 (nand_1_out, not_1_out, hit);
  nor nor_1 (user_hit, nand_1_out, user_lose);

  // Notes on the sheet:
  //   user
  //   Five_Cards_User
endmodule
